# Fritzing sketch jcscpu-hmc (saved by Fritzing 0.9.4)
breadboards: 16

parts:
  Part1 = Arduino Nano (Rev3.0) (ICSP)
  Part2 = Arduino Nano (Rev3.0) (ICSP)
  Part3 = Arduino Nano (Rev3.0) (ICSP)
  Part4 = Arduino Nano (Rev3.0) (ICSP)
  Part5 = Arduino Nano (Rev3.0) (ICSP)
  SW1 = DIP Switch 8 Position [package=dipswitch-08]
  LED41 = smd LED [color="Green (555nm)" package="1206 [SMD]"]
  S1 = Pushbutton [package="[SMD]"]
  U28 = 74HC595 [package="DIP16 [THT]"]
  U29 = 74HC595 [package="DIP16 [THT]"]
  U30 = 74HC595 [package="DIP16 [THT]"]
  U31 = 74HC595 [package="DIP16 [THT]"]
  R32 = Resistor [tolerance=±5% resistance=10k package="0402 [SMD]"]
  R33 = Resistor [tolerance=±5% resistance=10k package="0402 [SMD]"]
  R34 = Resistor [tolerance=±5% resistance=10k package="0402 [SMD]"]
  R35 = Resistor [tolerance=±5% resistance=10k package="0402 [SMD]"]
  R36 = Resistor [tolerance=±5% resistance=10k package="0402 [SMD]"]
  R37 = Resistor [tolerance=±5% resistance=10k package="0402 [SMD]"]
  R38 = Resistor [tolerance=±5% resistance=10k package="0402 [SMD]"]
  R5 = Resistor [tolerance=±5% resistance=1k package=THT]
  R7 = Resistor [tolerance=±5% resistance=1k package=THT]
  R6 = Resistor [tolerance=±5% resistance=1k package=THT]
  R4 = Resistor [tolerance=±5% resistance=1k package=THT]
  R3 = Resistor [tolerance=±5% resistance=1k package=THT]
  R2 = Resistor [tolerance=±5% resistance=1k package=THT]
  R8 = Resistor [tolerance=±5% resistance=1k package=THT]
  R1 = Resistor [tolerance=±5% resistance=1k package=THT]
  LED53 = smd LED [color="Green (555nm)" package="1206 [SMD]"]
  LED54 = smd LED [color="Green (555nm)" package="1206 [SMD]"]
  LED55 = smd LED [color="Green (555nm)" package="1206 [SMD]"]
  LED56 = smd LED [color="Green (555nm)" package="1206 [SMD]"]
  LED57 = smd LED [color="Green (555nm)" package="1206 [SMD]"]
  LED58 = smd LED [color="Green (555nm)" package="1206 [SMD]"]
  LED59 = smd LED [color="Green (555nm)" package="1206 [SMD]"]
  R39 = Resistor [tolerance=±5% resistance=10k package="0402 [SMD]"]
  SN74HC373 = IC, DIP package, 20 pins [chip_label=SN74HC373]
  SN74HC376 = IC, DIP package, 20 pins [chip_label=SN74HC373]
  SN74HC377 = IC, DIP package, 20 pins [chip_label=SN74HC373]
  SN74HC378 = IC, DIP package, 20 pins [chip_label=SN74HC373]
  SN74HC379 = IC, DIP package, 20 pins [chip_label=SN74HC373]
  SN74HC374 = IC, DIP package, 20 pins [chip_label=SN74HC373]
  SN74HC00 = IC, DIP package, 14 pins [chip_label=SN74HC00]
  SN74HC380 = IC, DIP package, 14 pins [chip_label=SN74HC00]
  SN74HC381 = IC, DIP package, 20 pins [chip_label=SN74HC373]
  R44 = Resistor [tolerance=±5% resistance=1k package=THT]
  R45 = Resistor [tolerance=±5% resistance=1k package=THT]
  R47 = Resistor [tolerance=±5% resistance=1k package=THT]
  R48 = Resistor [tolerance=±5% resistance=1k package=THT]
  R49 = Resistor [tolerance=±5% resistance=1k package=THT]
  R50 = Resistor [tolerance=±5% resistance=1k package=THT]
  R51 = Resistor [tolerance=±5% resistance=1k package=THT]
  R52 = Resistor [tolerance=±5% resistance=1k package=THT]
  R53 = Resistor [tolerance=±5% resistance=10k package="0402 [SMD]"]
  SN74HC383 = IC, DIP package, 14 pins [chip_label=SN74HC00]
  SN74HC04 = IC, DIP package, 14 pins [chip_label=SN74HC04]
  SN74HC32 = IC, DIP package, 14 pins [chip_label=SN74HC32]
  R54 = Resistor [tolerance=±5% resistance=1k package=THT]
  SN74HC384 = IC, DIP package, 14 pins [chip_label=SN74HC00]
  R41 = Resistor [tolerance=±5% resistance=1k package=THT]
  R42 = Resistor [tolerance=±5% resistance=1k package=THT]
  R55 = Resistor [tolerance=±5% resistance=1k package=THT]
  R56 = Resistor [tolerance=±5% resistance=1k package=THT]
  R57 = Resistor [tolerance=±5% resistance=1k package=THT]
  R58 = Resistor [tolerance=±5% resistance=1k package=THT]
  R59 = Resistor [tolerance=±5% resistance=1k package=THT]
  R60 = Resistor [tolerance=±5% resistance=1k package=THT]
  R61 = Resistor [tolerance=±5% resistance=1k package=THT]
  R62 = Resistor [tolerance=±5% resistance=1k package=THT]
  R63 = Resistor [tolerance=±5% resistance=1k package=THT]
  R64 = Resistor [tolerance=±5% resistance=1k package=THT]
  R65 = Resistor [tolerance=±5% resistance=1k package=THT]
  R66 = Resistor [tolerance=±5% resistance=1k package=THT]
  R67 = Resistor [tolerance=±5% resistance=1k package=THT]
  R68 = Resistor [tolerance=±5% resistance=1k package=THT]
  R69 = Resistor [tolerance=±5% resistance=1k package=THT]
  R70 = Resistor [tolerance=±5% resistance=1k package=THT]
  R71 = Resistor [tolerance=±5% resistance=1k package=THT]
  R72 = Resistor [tolerance=±5% resistance=1k package=THT]
  R73 = Resistor [tolerance=±5% resistance=1k package=THT]
  R74 = Resistor [tolerance=±5% resistance=1k package=THT]  # not connected
  R75 = Resistor [tolerance=±5% resistance=1k package=THT]
  R76 = Resistor [tolerance=±5% resistance=1k package=THT]
  R77 = Resistor [tolerance=±5% resistance=1k package=THT]
  R78 = Resistor [tolerance=±5% resistance=1k package=THT]
  R79 = Resistor [tolerance=±5% resistance=1k package=THT]
  R80 = Resistor [tolerance=±5% resistance=1k package=THT]
  R81 = Resistor [tolerance=±5% resistance=1k package=THT]
  LED60 = LED - 3mm [color="Red (633nm)" package="3 mm [THT]"]

nets:
  N1: Part1.D1/TX, Part5.D1/TX
  N2: Part1.D0/RX, Part5.D0/RX
  N3: Part1.RESET, Part5.RESET
  GND: Part1.GND, Part2.GND, Part3.GND, Part4.GND, Part5.GND, U28.GND, U28.OE, U29.GND, U29.OE, U30.GND, U30.OE, U31.GND, U31.OE, R5.Pin_0, R7.Pin_0, R6.Pin_0, R4.Pin_0, R3.Pin_0, R2.Pin_0, R8.Pin_0, R1.Pin_0, SN74HC373.pin1, SN74HC374.pin1, SN74HC374.pin10, SN74HC00.pin7, SN74HC380.pin7, SN74HC383.pin7, SN74HC384.pin7, R41.Pin_0, R42.Pin_0, R55.Pin_1, R56.Pin_1, R57.Pin_1, R58.Pin_1, R59.Pin_1, R60.Pin_1, R61.Pin_1, R62.Pin_1, R63.Pin_1, R64.Pin_1, R65.Pin_1, R66.Pin_1, R67.Pin_1, R68.Pin_1, R69.Pin_1, R70.Pin_1, R71.Pin_1, R72.Pin_1, R73.Pin_1, R75.Pin_1, R76.Pin_1, R77.Pin_1, R78.Pin_1, R79.Pin_1, R80.Pin_0, R81.Pin_0
  N4: Part1.D2, Part5.D2, U29.Q3
  N5: Part1.D3, Part5.D3, U29.Q2
  N6: Part1.D4, Part5.D4, U29.Q1
  N7: Part1.D5, Part5.D5, SW1.9, LED41.anode, R38.Pin_0, SN74HC373.pin2, SN74HC373.pin3, SN74HC376.pin2, SN74HC376.pin3, SN74HC377.pin2, SN74HC377.pin3, SN74HC378.pin3, SN74HC379.pin2, SN74HC379.pin3, SN74HC381.pin2, SN74HC381.pin3
  N8: Part1.D6, Part5.D6, SW1.10, R37.Pin_0, LED53.anode, SN74HC373.pin4, SN74HC373.pin5, SN74HC376.pin4, SN74HC376.pin5, SN74HC377.pin4, SN74HC377.pin5, SN74HC378.pin4, SN74HC379.pin4, SN74HC379.pin5, SN74HC381.pin4, SN74HC381.pin5
  N9: Part1.D7, Part5.D7, SW1.11, LED54.anode, R39.Pin_0, SN74HC373.pin6, SN74HC373.pin7, SN74HC376.pin6, SN74HC376.pin7, SN74HC377.pin7, SN74HC378.pin7, SN74HC379.pin7, SN74HC381.pin6, SN74HC381.pin7
  N10: Part1.D8, Part5.D8, SW1.12, R36.Pin_0, LED55.anode, SN74HC373.pin8, SN74HC373.pin9, SN74HC376.pin8, SN74HC376.pin9, SN74HC377.pin8, SN74HC377.pin9, SN74HC378.pin8, SN74HC379.pin8, SN74HC379.pin9, SN74HC381.pin8, SN74HC381.pin9
  N11: Part1.D9, Part5.D9, SW1.13, R34.Pin_0, LED56.anode, SN74HC377.pin12, SN74HC377.pin13, SN74HC379.pin12, SN74HC379.pin13
  N12: Part1.D10, Part5.D10, SW1.14, R35.Pin_0, LED57.anode, SN74HC377.pin14, SN74HC377.pin15, SN74HC379.pin14, SN74HC379.pin15
  N13: Part1.D11/MOSI, Part5.D11/MOSI, SW1.15, R33.Pin_0, LED59.anode, SN74HC377.pin16, SN74HC377.pin17, SN74HC379.pin16, SN74HC379.pin17
  N14: Part1.D12/MISO, Part5.D12/MISO, SW1.16, R32.Pin_0, LED58.anode, SN74HC377.pin18, SN74HC377.pin19, SN74HC379.pin18, SN74HC379.pin19
  VIN: Part1.VIN, Part5.VIN
  5V: Part1.5V, Part2.5V, Part3.5V, Part4.5V, Part5.5V, SW1.1, SW1.2, SW1.3, SW1.4, SW1.5, SW1.6, SW1.7, SW1.8, S1.Pin_1, S1.Pin_2, U28.MR, U28.VCC, U29.MR, U29.VCC, U30.MR, U30.VCC, U31.MR, U31.VCC, SN74HC377.pin20, SN74HC379.pin20, SN74HC374.pin20, SN74HC00.pin14, SN74HC380.pin14, SN74HC383.pin14, SN74HC04.pin14, SN74HC32.pin14, SN74HC384.pin14
  N15: Part1.A7, Part5.A7
  N16: Part1.A6, Part5.A6
  N17: Part1.A5, Part2.A5, Part3.A5, Part4.A5, Part5.A5
  N18: Part1.A4, Part2.A4, Part3.A4, Part4.A4, Part5.A4
  N19: Part1.A3, Part5.A3, U29.Q0
  N20: Part1.A2, Part5.A2, U28.SH_CP, U29.SH_CP, U30.SH_CP, U31.SH_CP
  N21: Part1.A1, Part5.A1, U28.ST_CP, U29.ST_CP, U30.ST_CP, U31.ST_CP
  N22: Part1.A0, Part5.A0, U29.DS
  N23: Part1.AREF, Part5.AREF
  3V3: Part1.3V3, Part5.3V3
  N24: Part1.D13/SCK, Part5.D13/SCK
  N25: Part2.D2, U28.Q3
  N26: Part2.D5, U28.Q2
  N27: Part2.D6, U28.Q1
  N28: Part2.D7, U28.Q0, SN74HC380.pin2, SN74HC380.pin12
  N29: Part2.D8, SN74HC00.pin11
  N30: Part2.D9, SN74HC374.pin8
  N31: Part2.D10, SN74HC374.pin7
  N32: Part2.D11/MOSI, SN74HC374.pin4
  N33: Part2.D12/MISO, SN74HC374.pin3
  N34: Part2.A2, U29.Q7
  N35: Part2.A1, U29.Q6
  N36: Part2.A0, U29.Q5
  N37: Part3.D3, LED60.cathode
  N38: Part3.D4, S1.Pin_3, S1.Pin_4, R53.Pin_1
  N39: Part3.A3, U30.Q3
  N40: Part3.A2, U30.Q2
  N41: Part3.A1, U30.Q1
  N42: Part3.A0, U30.Q0
  N43: Part4.D2, U31.Q2
  N44: Part4.D3, SN74HC32.pin3
  N45: Part4.D5, SN74HC04.pin4
  N46: Part4.D6, SN74HC04.pin1
  N47: Part4.D7, SN74HC04.pin10
  N48: Part4.D8, SN74HC04.pin13
  N49: Part4.A3, U31.Q1
  N50: LED41.cathode, R6.Pin_1
  N51: U28.Q5, SN74HC00.pin2
  N52: U28.Q6, SN74HC00.pin5, SN74HC00.pin6
  N53: U28.Q7', U30.DS
  N54: U28.DS, U29.Q7'
  N55: U30.Q4, SN74HC384.pin1, SN74HC384.pin2
  N56: U30.Q5, SN74HC384.pin4, SN74HC384.pin5
  N57: U30.Q7', U31.DS
  N58: U31.Q3, SN74HC383.pin1, SN74HC383.pin2
  N59: U31.Q4, SN74HC383.pin4, SN74HC383.pin5
  N60: U31.Q5, SN74HC377.pin11
  N61: R7.Pin_1, LED53.cathode
  N62: R4.Pin_1, LED55.cathode
  N63: R3.Pin_1, LED56.cathode
  N64: R2.Pin_1, LED57.cathode
  N65: R8.Pin_1, LED59.cathode
  N66: R1.Pin_1, LED58.cathode
  N67: SN74HC376.pin1, SN74HC384.pin6
  N68: SN74HC376.pin10, SN74HC378.pin1, SN74HC378.pin10, SN74HC379.pin10, SN74HC381.pin10, R44.Pin_0, R45.Pin_0, R47.Pin_0, R48.Pin_0, R49.Pin_0, R50.Pin_0, R51.Pin_0, R52.Pin_0, R53.Pin_0, R54.Pin_0
  N69: SN74HC377.pin1, SN74HC383.pin6
  N70: SN74HC379.pin1, SN74HC383.pin3
  N71: SN74HC374.pin2, SN74HC380.pin1
  N72: SN74HC00.pin1, SN74HC380.pin6, SN74HC380.pin9
  N73: SN74HC00.pin3, SN74HC00.pin12, SN74HC00.pin13
  N74: SN74HC380.pin3, SN74HC380.pin13
  N75: SN74HC380.pin4, SN74HC380.pin5, SN74HC380.pin8
  N76: SN74HC380.pin10, SN74HC380.pin11
  N77: SN74HC381.pin1, SN74HC384.pin3
  N78: R52.Pin_1, LED60.anode
  N79: SN74HC04.pin3, SN74HC32.pin4
  N80: SN74HC04.pin6, SN74HC32.pin5
  N81: SN74HC04.pin7, SN74HC32.pin7
  N82: SN74HC04.pin8, SN74HC32.pin11
  N83: SN74HC04.pin11, SN74HC32.pin9
  N84: SN74HC32.pin1, SN74HC32.pin8
  N85: SN74HC32.pin2, SN74HC32.pin6

notes:
  FLAGS
  R0
  R1
  R2
  R3
  HLT
  MAR_s
  RAM_s
  RAM_e
  IR
  ALU2
  ALU1
  ALU0
  Ctmp_e
  IAR_e
  IAR_s
  TMP_s
  ACC_s
  FLAGS_s
  BUS1
  ACC_e
  JCOND
  R0_e
  R1_e
  R0_s
  R1_s
  IR_s
  R2_e
  R3_e
  R3_s
  R2_s
  IO_s
  IO_e
  IO_io
  IAR
